# Fritzing sketch aquarium (saved by Fritzing 0.9.1b)
circuit board: 8.46667cm x 5.64444cm
breadboards: 1

parts:
  Tiny_RTC = Tiny RTC
  LCD1 = LCD screen
  R1 = Resistor [tolerance=±5% resistance=220 package=THT]
  Arduino_UNO = Arduino Uno (Rev3)
  R2 = Trimmer Potentiometer [maximum_resistance=10kΩ package=THT]
  T1 = TMP36 Temperature Sensor [package="TO92 [THT]"]
  C1 = Ceramic Capacitor [capacitance=100nF package="100 mil [THT, multilayer]"]
  S5 = Pushbutton [package="[THT]"]
  S4 = Pushbutton [package="[THT]"]
  S3 = Pushbutton [package="[THT]"]
  S2 = Pushbutton [package="[THT]"]
  S1 = Pushbutton [package="[THT]"]
  R7 = Resistor [tolerance=±5% resistance=2.2k package=THT]
  R6 = Resistor [tolerance=±5% resistance=1k package=THT]
  R5 = Resistor [tolerance=±5% resistance=680 package=THT]
  R4 = Resistor [tolerance=±5% resistance=330 package=THT]
  R3 = Resistor [tolerance=±5% resistance=2k package=THT]
  U1 = LM 358 Dual Op-Amp [package="DIP8 [THT]"]
  R8 = Resistor [tolerance=±5% resistance=220 package=THT]
  R9 = Resistor [tolerance=±5% resistance=10k package=THT]
  R10 = Resistor [tolerance=±5% resistance=500 package=THT]
  LED2 = LED - 5mm [color="Red (633nm)" package="5 mm [THT]"]
  LED3 = LED - 5mm [color="Yellow (585nm)" package="5 mm [THT]"]
  LED4 = LED - 5mm [color="Green (555nm)" package="5 mm [THT]"]
  LED5 = LED - 5mm [color="Blue (470nm)" package="5 mm [THT]"]
  R11 = Resistor [tolerance=±5% resistance=1k package=THT]
  R12 = Resistor [tolerance=±5% resistance=1k package=THT]
  R13 = Resistor [tolerance=±5% resistance=1k package=THT]
  R14 = Resistor [tolerance=±5% resistance=1k package=THT]
  LED1 = LED - 5mm [color="Green (570nm)" package="5 mm [THT]"]
  R15 = Resistor [tolerance=±5% resistance=1k package=THT]
  J1_-_18V = Power Jack [package=power_jack_smd]
  Power_LED9 = Power LED on star
  Power_LED4 = Power LED on star
  Power_LED1 = Power LED on star
  Power_LED7 = Power LED on star
  Power_LED6 = Power LED on star
  Power_LED3 = Power LED on star
  Power_LED5 = Power LED on star
  Power_LED2 = Power LED on star
  Power_LED8 = Power LED on star
  LDD-1000H1 = MeanWell LDD-1000H
  LDD-1000H2 = MeanWell LDD-1000H
  4_Relay_Module1 = 4 Relay Module
  Part1 = QSKJ DC-DC stepdown converter  # not connected

nets:
  N1: Tiny_RTC.SCL, Arduino_UNO.A5/SCL
  N2: Tiny_RTC.SDA, Arduino_UNO.A4/SDA
  5V: Tiny_RTC.VCC, LCD1.VDD, R1.Pin_0, Arduino_UNO.AREF, Arduino_UNO.5V, R2.leg2, T1.+Vs, C1.1, R3.Pin_0, U1.connector7, 4_Relay_Module1.VCC, 4_Relay_Module1.IN4
  GND: Tiny_RTC.GND, LCD1.VSS, LCD1.R/W, LCD1.LED-, Arduino_UNO.GND, R2.leg1, T1.GND, C1.0, S5.Pin_1, S5.Pin_2, S4.Pin_1, S4.Pin_2, S3.Pin_1, S3.Pin_2, S2.Pin_1, S2.Pin_2, S1.Pin_1, S1.Pin_2, U1.connector3, R8.Pin_0, R9.Pin_0, R11.Pin_0, R12.Pin_0, R13.Pin_0, R14.Pin_0, R15.Pin_0, 4_Relay_Module1.GND
  N3: LCD1.V0, R2.wiper
  N4: LCD1.RS, Arduino_UNO.D13/SCK
  N5: LCD1.E, Arduino_UNO.D12/MISO
  N6: LCD1.DB4, Arduino_UNO.D5_PWM
  N7: LCD1.DB5, Arduino_UNO.D4
  N8: LCD1.DB6, Arduino_UNO.D3_PWM
  N9: LCD1.DB7, Arduino_UNO.D2
  N10: LCD1.LED+, R1.Pin_1
  N11: Arduino_UNO.A0, U1.connector6, R9.Pin_1, R10.Pin_0
  N12: Arduino_UNO.A1, S1.Pin_3, S1.Pin_4, R4.Pin_0, R3.Pin_1
  Switch_2: Arduino_UNO.D8, LED5.anode, 4_Relay_Module1.IN2
  Switch_1: Arduino_UNO.D9_PWM, LED4.anode, 4_Relay_Module1.IN1
  Light_2: Arduino_UNO.D10_PWM/SS, LED3.anode, LDD-1000H2.PWM_DIM
  Light_1: Arduino_UNO.D11_PWM/MOSI, LED2.anode, LDD-1000H1.PWM_DIM
  N13: Arduino_UNO.D7, LED1.anode
  N14: T1.Vout, U1.connector4
  N15: S5.Pin_3, S5.Pin_4, R7.Pin_1
  N16: S4.Pin_3, S4.Pin_4, R7.Pin_0, R6.Pin_1
  N17: S3.Pin_3, S3.Pin_4, R6.Pin_0, R5.Pin_1
  N18: S2.Pin_3, S2.Pin_4, R5.Pin_0, R4.Pin_1
  N19: U1.connector5, R8.Pin_1, R10.Pin_1
  N20: LED2.cathode, R11.Pin_1
  N21: LED3.cathode, R12.Pin_1
  N22: LED4.cathode, R13.Pin_1
  N23: LED5.cathode, R14.Pin_1
  N24: LED1.cathode, R15.Pin_1
  N25: J1_-_18V.PWR, LDD-1000H1.+Vin, LDD-1000H2.+Vin
  N26: J1_-_18V.GND, LDD-1000H1.-Vin, LDD-1000H2.-Vin
  N27: Power_LED9.+, Power_LED8.-
  N28: Power_LED9.-, LDD-1000H2.-Vout
  N29: Power_LED4.+, Power_LED3.-
  N30: Power_LED4.-, LDD-1000H1.-Vout
  N31: Power_LED1.+, LDD-1000H1.+Vout
  N32: Power_LED1.-, Power_LED2.+
  N33: Power_LED7.+, Power_LED6.-
  N34: Power_LED7.-, Power_LED8.+
  N35: Power_LED6.+, Power_LED5.-
  N36: Power_LED3.+, Power_LED2.-
  N37: Power_LED5.+, LDD-1000H2.+Vout

notes:
  Light_1
  Light_2
  Switch_1
  Switch_2

custom parts:
  Tiny RTC: Tiny RTC I2C module DS1370Z RTC and AT24C32 EEPROM
  Power LED on star: PCB mounted RGB LED.
  MeanWell LDD-1000H: DC-DC Constant Current Step-Down LED drive
  4 Relay Module: a 4 relay module for Arduino or other
  QSKJ DC-DC stepdown converter: Description: This is a 2A stepdown converter - Brand: Jtron - Model: 03100125 - Color: Red - Material: Glass fiber - Module properties: Non-isolated step-down module (Buck) - Rectification: Non-synchronous - Input voltage: DC 4.5~35V - Output voltage: 1.25~30V (adjustable or fixed) - Rated current: 2A - Output current: Max. 3A; Suggest add heat sink if output power is over 15W - Conversion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
